# Fritzing sketch MiniDexed (saved by Fritzing 0.8.7b)

parts:
  RE1 = Rotary Encoder [package=THT]
  LCD1 = LCD screen
  Part1 = Arduino Midi Shield
  Raspberry_Pi_1 = Raspberry Pi 3
  Part2 = Adafruit UDA1334 I2S DAC [part_number="Adafruit #3678"]
  Part3 = Logic Level Converter

nets:
  N1: RE1.EncoderPinA, Raspberry_Pi_1.GIPO5
  N2: RE1.EncoderPinC, Raspberry_Pi_1.GIPO26
  N3: RE1.EncoderPinB, Raspberry_Pi_1.GIPO6
  GND: LCD1.VSS, Part1.GND, Raspberry_Pi_1.GND, Part2.GND, Part3.GND
  N4: LCD1.RS, Raspberry_Pi_1.GIPO27
  N5: LCD1.R/W, Raspberry_Pi_1.GIPO16
  N6: LCD1.E, Raspberry_Pi_1.GIPO17
  N7: LCD1.DB4, Raspberry_Pi_1.GIPO22
  N8: LCD1.DB5, Raspberry_Pi_1.GIPO23
  N9: LCD1.DB6, Raspberry_Pi_1.GIPO24
  N10: LCD1.DB7, Raspberry_Pi_1.GIPO25
  3.3V: Part1.3.3V, Raspberry_Pi_1.3v3, Part3.LV
  VCC: Part1.VCC, Raspberry_Pi_1.5V, Part2.VIN, Part3.HV
  N11: Part1.RX-I, Part3.RX_LV
  N12: Part1.TX, Part3.TX_LV
  N13: Raspberry_Pi_1.GIPO19, Part2.SFOR0
  N14: Raspberry_Pi_1.GIPO21, Part2.SFOR1
  N15: Raspberry_Pi_1.GIPO18, Part2.BITCLK_IN
  N16: Raspberry_Pi_1.GIPO15, Part3.RX_HV
  N17: Raspberry_Pi_1.GIPO14, Part3.TX_HV

custom parts:
  Adafruit UDA1334 I2S DAC: This fully-featured UDA1334A I2S Stereo DAC breakout is a perfect match for any I2S-output audio interface. It's affordable but sounds great! The NXP UDA1334A is a jack-of-all-I2S-trades: you can use 3.3V - 5V logic levels (a rarity), and can process multiple different formats by setting two pins to high or low. The DAC will process data immediately, and give you a clear, analog, stereo line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
